# Fritzing sketch SmartDesk (saved by Fritzing 0.9.4)
breadboards: 1

parts:
  Argon1 = Particle Argon
  WS2812B1 = WS2812B [package="DIP (Dual Inline) [THT]"]
  Load_Cell1 = Load Cell - Red/white/black/green
  Part1 = HX711 Weighing Sensor Module
  Part2 = Ambient Light Sensor (TEMT6000 Breakout Board)
  Part3 = Adafruit 2.8 inch Captouch TFT [part_number="Adafruit #2090"]
  Part4 = sensor_biometrico

nets:
  VCC: Argon1.3.3V, Part1.VCC, Part2.VCC, Part4.VCC
  GND: Argon1.GND, WS2812B1.GND, Part1.GND, Part2.GND, Part3.GND, Part4.GND
  N1: Argon1.A0, Part2.S
  N2: Argon1.A4, Part3.D/C_WR
  N3: Argon1.A5, Part3.CS
  N4: Argon1.SCK, Part3.C/D_CLK
  N5: Argon1.MO, Part3.MOSI
  N6: Argon1.MI, Part3.MISO
  N7: Argon1.RX, Part4.RX
  N8: Argon1.TX, Part4.TX
  N9: Argon1.SDA, Part3.SDA
  N10: Argon1.SCL, Part3.SCL
  N11: Argon1.D4, Part3.LITE
  N12: Argon1.D5, Part3.IRQ
  N13: Argon1.D6, Part1.DO/RX
  N14: Argon1.D7, Part1.CK/TX
  N15: Argon1.D8, WS2812B1.DI
  5V: Argon1.VUSB, WS2812B1.5V, Part3.VIN
  N16: Load_Cell1.wire1, Part1.E+
  N17: Load_Cell1.wire2, Part1.A+
  N18: Load_Cell1.wire3, Part1.E-
  N19: Load_Cell1.wire4, Part1.A-

custom parts:
  Particle Argon: The Argon is a powerful Wi-Fi enabled development board that can act as either a standalone Wi-Fi endpoint or Wi-Fi enabled gateway for Particle Mesh networks. It is based on the Nordic nRF52840 and has built-in battery charging circuitry so it’s easy to connect a Li-Po and deploy your local network in minutes. The Argon is great for connecting existing projects to the Particle Device Cloud or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
  WS2812B: Adafruit NeoPixel Breakout
  Load Cell - Red/white/black/green: A rectangle load cell/weighting pressure Sensor with four wires - Red, white, black, green. Normally corresponding with E+, E-, A+, A- respectively.
  Adafruit 2.8 inch Captouch TFT: Add some jazz & pizazz to your project with a color capactive touchscreen LCD. This TFT display is big (2.8" diagonal) bright (4 white-LED backlight) and colorful! 240x320 pixels with individual RGB pixel control, this has way more resolution than a black and white 128x64 display. As a bonus, this display has a capacitive single-touch touchscreen attached to it already, so you can detect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
  sensor_biometrico: Adafruit Optical Fingerprint Sensor
